// Logisim project codificador.circ as structural Verilog: 1 circuit, main circuit main
module main (
  input  V7,
  input  V6,
  input  V5,
  input  V4,
  input  V3,
  input  V2,
  input  V1,
  output s2,
  output s1,
  output s0
);

  wire and_1_out, and_2_out, and_3_out, and_4_out, not_2_out, not_3_out, not_4_out, not_5_out, or_2_out,
       or_3_out;

  not not_1 (s2, V4);
  not not_2 (not_2_out, V4);
  not not_3 (not_3_out, V2);
  not not_4 (not_4_out, V4);
  not not_5 (not_5_out, V6);
  and and_1 (and_1_out, not_2_out, V2);
  and and_2 (and_2_out, not_3_out, V1);
  and and_3 (and_3_out, not_4_out, V3);
  and and_4 (and_4_out, not_5_out, V5);
  or or_1 (s1, and_1_out, V6);
  or or_2 (or_2_out, and_2_out, and_3_out);
  or or_3 (or_3_out, and_4_out, V7);
  or or_4 (s0, or_2_out, or_3_out);
endmodule
