// Logisim project decodificador.circ as structural Verilog: 1 circuit, main circuit main
module main (
  input  s2,
  input  s1,
  input  s0,
  output V7,
  output V6,
  output V5,
  output V4,
  output V3,
  output V2,
  output V1,
  output V0
);

  wire not_1_out, not_2_out, not_3_out, not_4_out, not_5_out, not_6_out, not_7_out, not_8_out, not_9_out,
       not_10_out, not_11_out, not_12_out;

  not not_1 (not_1_out, s2);
  not not_2 (not_2_out, s2);
  not not_3 (not_3_out, s0);
  not not_4 (not_4_out, s2);
  not not_5 (not_5_out, s1);
  not not_6 (not_6_out, s2);
  not not_7 (not_7_out, s1);
  not not_8 (not_8_out, s0);
  not not_9 (not_9_out, s0);
  not not_10 (not_10_out, s1);
  not not_11 (not_11_out, s1);
  not not_12 (not_12_out, s0);
  and and_1 (V7, not_1_out, s1, s0);
  and and_2 (V6, not_2_out, s1, not_3_out);
  and and_3 (V5, not_4_out, not_5_out, s0);
  and and_4 (V4, not_6_out, not_7_out, not_8_out);
  and and_5 (V3, s2, s1, s0);
  and and_6 (V2, s2, s1, not_9_out);
  and and_7 (V1, s2, not_10_out, s0);
  and and_8 (V0, s2, not_11_out, not_12_out);
endmodule
